// Logisim project two_bit_input_ripple_carry_adder.circ as structural Verilog: 2 circuits, main circuit main
module main (
  input  x,
  input  in_2,
  input  y,
  input  in_4,
  output Output,
  output out_6,
  output x___y
);

  wire FA1_cout;

  FA FA2 (.Cout(Output), .S(out_6), .x(x), .y(y), .Cin(FA1_cout));
  FA FA1 (.Cout(FA1_cout), .S(x___y), .x(in_2), .y(in_4), .Cin(1'b0));

  // Notes on the sheet:
  //   Input:
  //   A 2-bit input ripple-carry adder
  //   Example how you do an abstract operation like addition using circuits
endmodule

module FA (
  input  x,
  input  y,
  input  Cin,
  output Cout,
  output S
);

  wire and_1_out, and_2_out, xor_2_out;

  or or_1 (Cout, and_1_out, and_2_out);
  and and_1 (and_1_out, Cin, y);
  and and_2 (and_2_out, x, xor_2_out);
  xor xor_1 (S, x, xor_2_out);
  xor xor_2 (xor_2_out, y, Cin);

  // Notes on the sheet:
  //   (Carrry over output)
  //   Full Adder
  //   (OR gate)
  //   (AND gate)
  //   (last digit sum for final output)
  //   (XOR gate)
  //   (Carrry over input)
endmodule
